// Logisim project 8bit_CPU.circ as structural Verilog: 2 circuits, main circuit main
module main (
  input  in_1,
  input  in_2,
  output [7:0] D0_7pins
);

  wire ACR, ADD_ADL, ADD_SB06, ADD_SB7, adder_1_cout, adder_2_cout, ADH_ABH, ADH_PCH, ADL_ABL, ADL_ADD,
       ADL_PCL, and_1_out, and_3_out, ANDS, bitselector_1_out, CL1, CL2, DB_ADD, DBx_ADD, DDA,
       decoder_1_out0, decoder_1_out1, DL_ADH, DL_ADL, DL_DB, DSA, EORS, I_ADDC, I_PC, O_ADD, O_ADH0,
       O_ADH17, O_ADL0, O_ADL1, O_ADL2, or_8_out, or_9_out, or_12_out, or_13_out, ORS, PCH_ADH, PCH_DB,
       PCH_PCH, PCL_ADL, PCL_DB, PCL_PCL, pull_resistor_1_node, pull_resistor_3_node, S_ADL, S_SB, SB_ADD,
       SB_ADH, SB_DB, SB_S, SRS, SUMS;
  wire [2:0] bit_extender_1_out;
  wire [3:0] counter_1_q;
  wire [6:0] controlled_buffer_24_out, pull_resistor_4_node;
  wire [7:0] ADD_q, adder_1_out, adder_2_out, adder_3_out, AI_q, and_2_out, BI_q, bit_extender_2_out,
       controlled_buffer_2_out, controlled_buffer_3_out, controlled_buffer_6_out, controlled_buffer_9_out,
       controlled_buffer_14_out, controlled_buffer_19_out, controlled_buffer_26_out,
       controlled_buffer_29_out, DL_q, DOR_q, IR_q, not_2_out, or_10_out, PCH_q, PCHS_q, PCL_q, PCLS_q, PD_q,
       pull_resistor_2_node, S_q, shifter_1_out, undriven, xor_1_out;
  wire [7:7] controlled_buffer_25_out;
  wire [15:0] ADB;
  wire [63:5] pla_1_out;

  Clock clock_1 (.out(CL1));
  Register IR (.D(PD_q), .en(decoder_1_out1), .clk(CL1), .Q(IR_q), .clr(in_1));
  not not_1 (CL2, CL1);
  Counter #(.max('h7), .width(3)) counter_1 (
    .clr(in_1), .up(1'b1), .count(1'b1), .clk(CL2), .Q(counter_1_q[2:0]));  // open: load, D, carry
  PLA #(.in_width(12), .out_width(64), .\table ("000000000000 0000000000000000000000000000000000000000000000000000000000000000")) pla_1 (
    .in({IR_q, counter_1_q}),
    .out({pla_1_out[63:40], SB_ADD, O_ADD, ADD_SB7, ADD_SB06, ADD_ADL, SRS, ORS, EORS, ANDS, SUMS, DSA, DDA, I_ADDC, ADL_ADD, DB_ADD, DBx_ADD, S_SB, SB_S, S_ADL, O_ADL2, O_ADL1, O_ADL0, SB_DB, SB_ADH, pla_1_out[15], PCH_DB, ADH_PCH, pla_1_out[12:11], PCL_DB, pla_1_out[9], ADL_PCL, pla_1_out[7:5], O_ADH17, O_ADH0, DL_ADH, DL_ADL, DL_DB}));
  Register PD (.D(D0_7pins), .en(CL2), .clk(CL2), .Q(PD_q), .clr(in_1));
  Decoder #(.enable("false"), .select(3)) decoder_1 (
    .out0(decoder_1_out0), .out1(decoder_1_out1), .sel(counter_1_q[2:0]));  // open: out2, out3, out4, out5, out6, out7
  RAM #(.addrWidth(16), .enables("line")) ram_1 (.addr(ADB), .we(in_2), .clk(CL1), .din(D0_7pins), .dout(D0_7pins));
  Register DOR (.D(controlled_buffer_2_out), .en(CL1), .clk(CL1), .Q(DOR_q), .clr(in_1));
  assign D0_7pins = in_2 ? DOR_q : 8'bz;  // Controlled_Buffer controlled_buffer_1
  or or_1 (ADH_ABH, pla_1_out[5], decoder_1_out0);
  or or_2 (ADL_ABL, pla_1_out[6], decoder_1_out0);
  or or_3 (PCL_PCL, pla_1_out[7], decoder_1_out0);
  or or_4 (I_PC, pla_1_out[9], decoder_1_out1);
  or or_5 (PCL_ADL, pla_1_out[11], decoder_1_out0);
  or or_6 (PCH_PCH, pla_1_out[12], decoder_1_out0);
  or or_7 (PCH_ADH, pla_1_out[15], decoder_1_out0);
  assign controlled_buffer_2_out = DL_DB ? undriven : 8'bz;  // Controlled_Buffer controlled_buffer_2
  assign not_2_out = ~controlled_buffer_2_out;  // NOT_Gate not_2, 8 bits wide
  assign controlled_buffer_3_out = DBx_ADD ? not_2_out : 8'bz;  // Controlled_Buffer controlled_buffer_3
  and and_1 (and_1_out, SUMS, adder_1_cout);
  assign controlled_buffer_2_out = PCL_DB ? PCL_q : 8'bz;  // Controlled_Buffer controlled_buffer_4
  assign controlled_buffer_3_out = DB_ADD ? controlled_buffer_2_out : 8'bz;  // Controlled_Buffer controlled_buffer_5
  Adder adder_1 (.a(BI_q), .b(AI_q), .out(adder_1_out), .cin(I_ADDC), .cout(adder_1_cout));
  assign bit_extender_1_out = {{2{1'b0}}, 1'b1};  // Bit_Extender bit_extender_1
  Register AI (.D(controlled_buffer_19_out), .en(or_12_out), .clk(CL1), .Q(AI_q), .clr(in_1));
  Register DL (.D(D0_7pins), .en(CL2), .clk(CL2), .Q(DL_q), .clr(in_1));
  or or_8 (or_8_out, ADL_PCL, PCL_PCL);
  assign controlled_buffer_6_out = PCL_PCL ? PCL_q : 8'bz;  // Controlled_Buffer controlled_buffer_6
  or or_9 (or_9_out, DBx_ADD, DB_ADD, ADL_ADD);
  BitSelector bitselector_1 (.in(AI_q), .out(bitselector_1_out), .sel(3'b000));
  assign controlled_buffer_6_out = ADL_PCL ? controlled_buffer_14_out : 8'bz;  // Controlled_Buffer controlled_buffer_7
  Register PCLS (.D(controlled_buffer_6_out), .en(or_8_out), .clk(CL1), .Q(PCLS_q), .clr(in_1));
  assign bit_extender_2_out = {{7{1'b0}}, I_PC};  // Bit_Extender bit_extender_2
  Register PCL (.D(adder_2_out), .en(CL2), .clk(CL2), .Q(PCL_q), .clr(in_1));
  assign controlled_buffer_3_out = ADL_ADD ? controlled_buffer_14_out : 8'bz;  // Controlled_Buffer controlled_buffer_8
  Register BI (.D(controlled_buffer_3_out), .en(or_9_out), .clk(CL1), .Q(BI_q), .clr(in_1));
  assign controlled_buffer_9_out = SUMS ? adder_1_out : 8'bz;  // Controlled_Buffer controlled_buffer_9
  assign and_2_out = BI_q & AI_q;  // AND_Gate and_2, 8 bits wide
  assign controlled_buffer_9_out = ANDS ? and_2_out : 8'bz;  // Controlled_Buffer controlled_buffer_10
  assign xor_1_out = BI_q ^ AI_q;  // XOR_Gate xor_1, 8 bits wide
  assign controlled_buffer_9_out = EORS ? xor_1_out : 8'bz;  // Controlled_Buffer controlled_buffer_11
  assign or_10_out = BI_q | AI_q;  // OR_Gate or_10, 8 bits wide
  assign controlled_buffer_9_out = ORS ? or_10_out : 8'bz;  // Controlled_Buffer controlled_buffer_12
  assign controlled_buffer_9_out = SRS ? shifter_1_out : 8'bz;  // Controlled_Buffer controlled_buffer_13
  Shifter #(.shift("lr")) shifter_1 (.in(AI_q), .\dist (bit_extender_1_out), .out(shifter_1_out));
  and and_3 (and_3_out, bitselector_1_out, SRS);
  or or_11 (ACR, and_1_out, and_3_out);
  Adder adder_2 (.a(PCLS_q), .b(bit_extender_2_out), .out(adder_2_out), .cout(adder_2_cout));  // open: cin
  assign controlled_buffer_14_out[0] = O_ADL0 ? pull_resistor_1_node : 1'bz;  // Controlled_Buffer controlled_buffer_14
  assign controlled_buffer_14_out[1] = O_ADL1 ? pull_resistor_1_node : 1'bz;  // Controlled_Buffer controlled_buffer_15
  assign controlled_buffer_14_out[2] = O_ADL2 ? pull_resistor_1_node : 1'bz;  // Controlled_Buffer controlled_buffer_16
  Pull_Resistor pull_resistor_1 (.node(pull_resistor_1_node));
  assign controlled_buffer_14_out = DL_ADL ? DL_q : 8'bz;  // Controlled_Buffer controlled_buffer_17
  assign controlled_buffer_14_out = PCL_ADL ? PCL_q : 8'bz;  // Controlled_Buffer controlled_buffer_18
  Register ADD (.D(controlled_buffer_9_out), .en(CL2), .clk(CL2), .Q(ADD_q));  // open: clr
  Pull_Resistor pull_resistor_2 (.node(pull_resistor_2_node));
  or or_12 (or_12_out, O_ADD, SB_ADD);
  assign controlled_buffer_19_out = O_ADD ? pull_resistor_2_node : 8'bz;  // Controlled_Buffer controlled_buffer_19
  assign controlled_buffer_14_out = ADD_ADL ? ADD_q : 8'bz;  // Controlled_Buffer controlled_buffer_20
  assign controlled_buffer_19_out = SB_ADD ? {controlled_buffer_25_out[7], controlled_buffer_24_out} : 8'bz;  // Controlled_Buffer controlled_buffer_21
  or or_13 (or_13_out, ADH_PCH, PCH_PCH);
  assign controlled_buffer_2_out = PCL_DB ? PCH_q : 8'bz;  // Controlled_Buffer controlled_buffer_22
  assign controlled_buffer_14_out = S_ADL ? S_q : 8'bz;  // Controlled_Buffer controlled_buffer_23
  assign controlled_buffer_24_out = ADD_SB06 ? ADD_q[6:0] : 7'bz;  // Controlled_Buffer controlled_buffer_24
  assign controlled_buffer_25_out[7] = ADD_SB7 ? ADD_q[7] : 1'bz;  // Controlled_Buffer controlled_buffer_25
  assign controlled_buffer_26_out = ADH_PCH ? controlled_buffer_29_out : 8'bz;  // Controlled_Buffer controlled_buffer_26
  assign controlled_buffer_26_out = PCH_PCH ? PCH_q : 8'bz;  // Controlled_Buffer controlled_buffer_27
  Register PCHS (.D(controlled_buffer_26_out), .en(or_13_out), .clk(CL1), .Q(PCHS_q), .clr(in_1));
  Register PCH (.D(adder_3_out), .en(CL2), .clk(CL2), .Q(PCH_q), .clr(in_1));
  assign controlled_buffer_2_out = SB_DB ? {controlled_buffer_25_out[7], controlled_buffer_24_out} : 8'bz;  // Controlled_Buffer controlled_buffer_28
  Register S (.D({controlled_buffer_25_out[7], controlled_buffer_24_out}), .en(SB_S), .clk(CL1), .Q(S_q), .clr(in_1));
  Adder adder_3 (.a(PCHS_q), .b({8{1'b0}}), .out(adder_3_out), .cin(adder_2_cout));  // open: cout
  assign controlled_buffer_29_out = DL_ADH ? undriven : 8'bz;  // Controlled_Buffer controlled_buffer_29
  assign controlled_buffer_29_out = PCH_ADH ? PCH_q : 8'bz;  // Controlled_Buffer controlled_buffer_30
  assign controlled_buffer_29_out = SB_ADH ? {controlled_buffer_25_out[7], controlled_buffer_24_out} : 8'bz;  // Controlled_Buffer controlled_buffer_31
  assign {controlled_buffer_25_out[7], controlled_buffer_24_out} = S_SB ? S_q : 8'bz;  // Controlled_Buffer controlled_buffer_32
  Register ABH (.D(controlled_buffer_29_out), .en(ADH_ABH), .clk(CL1), .Q(ADB[15:8]), .clr(in_1));
  assign controlled_buffer_29_out[7:1] = O_ADH17 ? pull_resistor_4_node : 7'bz;  // Controlled_Buffer controlled_buffer_33
  Register ABL (.D(controlled_buffer_14_out), .en(ADL_ABL), .clk(CL1), .Q(ADB[7:0]), .clr(in_1));
  Pull_Resistor pull_resistor_3 (.node(pull_resistor_3_node));
  assign controlled_buffer_29_out[0] = O_ADH0 ? pull_resistor_3_node : 1'bz;  // Controlled_Buffer controlled_buffer_34
  Pull_Resistor pull_resistor_4 (.node(pull_resistor_4_node));

  // Other names for the same wires on the sheet: RST = in_1; RW = in_2
endmodule

module ALU (
  input  [7:0] RegA,
  input  [7:0] RegB,
  input  Su,
  output [7:0] out_4
);

  wire adder_1_cout;
  wire [7:0] bit_extender_1_out, xor_1_out;

  assign bit_extender_1_out = {{7{Su}}, Su};  // Bit_Extender bit_extender_1
  assign xor_1_out = RegB ^ bit_extender_1_out;  // XOR_Gate xor_1, 8 bits wide
  Adder adder_1 (.a(RegA), .b(xor_1_out), .out(out_4), .cin(Su), .cout(adder_1_cout));
endmodule
